# Fritzing sketch Untitled Sketch 2 (saved by Fritzing 0.9.3b)
breadboards: 1

parts:
  MCU1 = Raspberry Pi Zero
  GSM_SIM_GPSR_SMS_SIM900_SIM1 = SIM800L [package=THT]
  VCC1 = Battery block 9V

nets:
  N1: MCU1.pin_2, MCU1.pin_4, GSM_SIM_GPSR_SMS_SIM900_SIM1.5V, VCC1.+
  N2: MCU1.pin_6, MCU1.pin_30, GSM_SIM_GPSR_SMS_SIM900_SIM1.GND, VCC1.-
  N3: MCU1.pin_8, GSM_SIM_GPSR_SMS_SIM900_SIM1.SIM_RXD
  N4: MCU1.pin_10, GSM_SIM_GPSR_SMS_SIM900_SIM1.SIM_TXD
